# Fritzing sketch Sketch_DHT_Notification (saved by Fritzing 0.9.0b)

parts:
  Part1 = ESPresso LIte V2.0
  DHT1 = DHT11 Humitidy and Temperature Sensor
  FTDI1 = FTDI Friend

nets:
  N1: Part1.no_name_yet#connector_CTS0, FTDI1.CTS
  N2: Part1.no_name_yet#connector_DTR0, FTDI1.RTS
  N3: Part1.no_name_yet#connector_GND3, FTDI1.GND
  N4: Part1.no_name_yet#connector_GND5, DHT1.GND
  N5: Part1.no_name_yet#connector_I121, DHT1.DATA
  N6: Part1.no_name_yet#connector_RX0, FTDI1.TX
  N7: Part1.no_name_yet#connector_TX0, FTDI1.RX
  N8: Part1.no_name_yet#connector_V33, DHT1.VDD
  N9: Part1.no_name_yet#connector_VIN2, FTDI1.VCC

custom parts:
  DHT11 Humitidy and Temperature Sensor: DHT11 Humidity and Temperature Sensor
