# Fritzing sketch Sketch_Soil_Relay (saved by Fritzing 0.9.0b)

parts:
  Part1 = ESPresso LIte V2.0
  KY-1 = Keyes Relay [package=THT]
  J1 = female pin header, 4 pins [form="♀ (female)"]

nets:
  N1: Part1.no_name_yet#connector_GND0, KY-1.ground
  N2: Part1.no_name_yet#connector_GND1, J1.pin3
  N3: Part1.no_name_yet#connector_I13, J1.pin2
  N4: Part1.no_name_yet#connector_I14, KY-1.signal
  N5: Part1.no_name_yet#connector_V3, KY-1.power, J1.pin4

custom parts:
  Keyes Relay: The Keyes 5V relay module is suitable for SCM development, home appliance control. It uses a 5V~12V TIL control signal which can control DC / AC signal.
